# Fritzing sketch Click-Circuits (saved by Fritzing 0.9.7b)

parts:
  J1 = Basic Force Sensing Resistor (FSR) [package=THT]
  U2 = ESP32-38PinWide [part_number=ESP32-38PinWide]
  Mod1 = AD8232 HeartRate Monitor [part_number=SEN-12650]
  U3 = LIPO-110mAh [package=lipo-110]
  元件4 = PowerBoost 500 Charger
  R2 = Basic Flex Resistor
  R3 = Resistor [tolerance=±5% resistance=220 package="2512 [SMD]"]  # not connected
  元件8 = BME280 Breakout
  RGB_SMD_LED1 = SMD RGB LED (WS2812) [package=5050]
  RGB_SMD_LED2 = SMD RGB LED (WS2812) [package=5050]  # not connected
  RGB_SMD_LED3 = SMD RGB LED (WS2812) [package=5050]  # not connected
  RGB_SMD_LED4 = SMD RGB LED (WS2812) [package=5050]  # not connected
  RGB_SMD_LED5 = SMD RGB LED (WS2812) [package=5050]  # not connected
  RGB_SMD_LED6 = SMD RGB LED (WS2812) [package=5050]  # not connected
  DFRobot_DFPlayer_Mini1 = DFRobot DFPlayer Mini [part_number=DFR0299]
  SPKR1 = Loudspeaker
  R4 = Resistor [tolerance=±5% resistance=10000 package="0805 [SMD]"]
  R5 = Resistor [tolerance=±5% resistance=10000 package="0805 [SMD]"]  # not connected
  R6 = Resistor [tolerance=±5% resistance=10000 package="0805 [SMD]"]  # not connected
  R7 = Resistor [tolerance=±5% resistance=220 package="2010 [SMD]"]  # not connected

nets (from the schematic view):
  N1: J1.pin_0, R4.Pin_0
  VCC: J1.pin_1, U2.VIN, 元件4.5.0V, R2.pin_1, 元件8.3.3V, RGB_SMD_LED1.VCC, DFRobot_DFPlayer_Mini1.VCC
  N2: U2.3.3, Mod1.3.3v
  N3: U2.GPIO36, U2.GPIO39, Mod1.OUTPUT, Mod1.LO-, Mod1.LO+, RGB_SMD_LED1.DIn
  N4: U2.GPIO34, U2.GPIO35
  GND: U2.GPIO32, U2.GPIO33, Mod1.GND, 元件8.GND
  N5: U2.GPIO16, DFRobot_DFPlayer_Mini1.TX
  N6: U2.GPIO17, DFRobot_DFPlayer_Mini1.RX
  N7: U2.GPIO21, 元件8.SDI/SDA
  N8: U2.GPIO22, 元件8.SCK/SCL
  N9: U3.+, 元件4.VBAT_OUT
  N10: U3.-, 元件4.GND, RGB_SMD_LED1.DOut, DFRobot_DFPlayer_Mini1.GND-1, DFRobot_DFPlayer_Mini1.GND-2, R4.Pin_1
  N11: DFRobot_DFPlayer_Mini1.SPK_1, SPKR1.pin1
  N12: DFRobot_DFPlayer_Mini1.SPK_2, SPKR1.pin2

custom parts:
  ESP32-38PinWide: Generic 38-Pin ESP32 with wide format (only access to one side of pins on a breadboard) based on Stephen Lilley's HiLetgo ESP-WROOM-32 ESP32 ESP-32S Development Board.
  AD8232 HeartRate Monitor: Sparkfun single lead heart rate monitor - Ad8232.
